# Fritzing sketch S_nodemcu_http_bt_ir_server_16servos_v1 (saved by Fritzing 0.9.3b)

parts:
  U1 = NodeMCU V3.0
  Componente1 = Bluetooth HC-05 Macho
  PWM1 = PCA9685 16x12-bit PWM Breakout
  DS1 = DS18B20 1-Wire Temperature Sensor [part_number=DS18B20]
  BAT1 = BC9VPC [package=bc9vpc]
  J1 = Basic Servo  # not connected
  J2 = Basic Servo  # not connected
  J3 = Basic Servo  # not connected
  J4 = Basic Servo  # not connected

nets:
  N1: U1.D1, PWM1.no_name_yet#504
  N2: U1.D2, PWM1.no_name_yet#503
  N3: U1.D6, DS1.GND
  N4: U1.RX, Componente1.TXD
  N5: U1.TX, Componente1.RXD
  N6: PWM1.no_name_yet#501, PWM1.no_name_yet#701, PWM1.no_name_yet#1000, PWM1.no_name_yet#1001, PWM1.no_name_yet#1002, PWM1.no_name_yet#1003, BAT1.V-
  N7: PWM1.no_name_yet#706, BAT1.V+

notes:
  BT - NodeMCU
  <module fritzingVersion="0.9.3b.04.19.5c895d327c44a3114e5fcc9d8260daf0cbb52806">
  <boundingRects>
  <boundingRect rect="302.922 -165.995 103.619 82.5322" name="Vista de Protoboard (placa de Prototipos)"/>
  <boundingRect rect="74.7 182.7 30.6 12.6" name="Vista de PCB"/>
  <boundingRect rect="-197.999 134.789 54 58.875" name="Vista de Esquemático"/>
  </boundingRects>
  <instances>
  <instance moduleIdRef="3234DBDC80leg" modelIndex="85431247" path="C:/Users/usuario/Downloads/fritzing.0.9.3b.64.pc/fritzing.0.9.3b.64.pc/fritzing-parts/core/servo.fzp">
  <title>J1</title>
  <views>
  <breadboardView layer="breadboard">
  <geometry z="3.00011" x="302.922" y="-165.995"/>
  <connectors>
  <connector layer="breadboard" connectorId="connector2">
  <geometry x="100.755" y="58.2421"/>
  <leg>
  <point x="0" y="0"/>
  <bezier/>
  <point x="1.32303" y="-0.2466"/>
  <bezier/>
  </leg>
  </connector>
  <connector layer="breadboard" connectorId="connector1">
  <geometry x="100.9" y="66.6868"/>
  <leg>
  <point x="0" y="0"/>
  <bezier/>
  <point x="1.17813" y="0.3087"/>
  <bezier/>
  </leg>
  </connector>
  <connector layer="breadboard" connectorId="connector0">
  <geometry x="100.617" y="75.0955"/>
  <leg>
  <point x="0" y="0"/>
  <bezier/>
  <point x="1.46073" y="0.9"/>
  <bezier/>
  </leg>
  </connector>
  </connectors>
  </breadboardView>
  <schematicView layer="schematic">
  <geometry z="3.0001" x="-200.437" y="137.226">
  <transform m32="-2.43752" m12="1" m31="56.4375" m33="1" m23="0" m21="-1" m22="0" m11="0" m13="0"/>
  </geometry>
  <titleGeometry x="-141.562" z="7.00011" textColor="#000000" yOffset="-7" xOffset="58.875" fontSize="5" visible="true" y="130.226">
  <displayKey key=""/>
  <displayKey key="part number"/>
  </titleGeometry>
  </schematicView>
  <pcbView layer="copper0">
  <geometry z="6.0001" x="83.7" y="173.7">
  <transform m32="9" m12="1" m31="21.6" m33="1" m23="0" m21="-1" m22="0" m11="0" m13="0"/>
  </geometry>
  <titleGeometry x="96.3" z="13.0001" textColor="#000000" yOffset="-7" xOffset="12.6" fontSize="5" visible="true" y="166.7">
  <displayKey key=""/>
  </titleGeometry>
  </pcbView>
  </views>
  </instance>
  </instances>
  </module>
  tx - rx
  rx -tx
  PCA9665 -NodeMCU
  SDA - D1
  SCL - D2
  PIN VU
  NodeMCU V++
  GND
  PIN VU
  NodeMCU
  V++
  GND

custom parts:
  NodeMCU V3.0: ESP8266 based NodeMCU

// code stored in the sketch: NodemcuTemperatureRelayLcd.ino
/********************** LYBRARY ****************************/

#define BLYNK_PRINT Serial // Comment this out to disable prints and save space


#include <ESP8266WiFi.h>
#include <BlynkSimpleEsp8266.h>
#include <OneWire.h>
#include <DallasTemperature.h>
#include <LiquidCrystal_I2C.h>

/* TIMER */
#include <SimpleTimer.h>
SimpleTimer timer;

/********************** BLYNK ACCOUNT ****************************/
char auth[] = "BLYNK_TOKEN";
char ssid[] = "SSID";
char pass[] = "PASS";


/********************** HARDWARE ****************************/
// Temperature sensor full ID, including family code and CRC
// use OneWire Scanner to get the address
DeviceAddress tempSensor = { 0x28, 0xFF, 0x64, 0x1D, 0x8F, 0x87, 0x95, 0xB1 };

// Pin used for the OneWire interface
#define ONE_WIRE_BUS 14 //pin D5 nodemcu Lolin v3

LiquidCrystal_I2C lcd(0x27, 16, 2); //LCD address and type.
//D2 = SDA D1 = SCL

/**************BIG CHAR*********************************************/


/********************** TEMPERATURE DEF****************************/
OneWire oneWire(ONE_WIRE_BUS);
DallasTemperature DS18B20(&oneWire);
float temp;

/********************** SETUP ****************************/
void setup()
{
  // Debug console
  Serial.begin(9600);
  Blynk.begin(auth, ssid, pass, IPAddress(188,166,206,43), 8080); //use other method to connect to blynk server
  DS18B20.begin();
  timer.setInterval(15000L, getSendData);
  Blynk.syncAll();

  pinMode(2, OUTPUT);
  
  lcd.init();
  lcd.backlight();
  lcd.clear();

}

/********************** LOOP ****************************/
void loop()
{
  Blynk.run();
  timer.run();
}

/********************** Send Sensor data to Blynk ****************************/
void getSendData()
{
  DS18B20.requestTemperatures(); 
  temp = DS18B20.getTempCByIndex(0);
  Serial.println(temp);
  Blynk.virtualWrite(10, temp); //virtual pin V10
  
  lcd.setCursor(0, 0);
  lcd.print("Temp:");
  lcd.setCursor(6,0);
  lcd.print(temp);
  lcd.setCursor(12,0);
  lcd.print("'C");
}
